# Fritzing sketch HitagiExpansionBoard (saved by Fritzing 0.9.5d)
circuit board: 10.5cm x 13cm
breadboards: 1

parts:
  STEMMA = female pin header, 4 pins [form="♀ (female)"]
  BAT1 = BC9VPC [package=bc9vpc]
  POWER = Toggle Switch [package=THT]
  STEMMA1 = Adafruit Stemma 4 pin header [form="♀ (female)" package=THT]
  PWM(3) = female pin header, 3 pins [form="♀ (female)"]
  Part1 = TFT 2.2 inch 320x240 w microSD [part_number=1480]
  PWM12 = LED - 5mm [color="Red (633nm)" package="5 mm [THT]"]
  RESET = Pushbutton [package="[SMD]"]
  SPI1 = JST PH SPI HEADER [form="♀ (female)" package=THT]
  PWM(4) = female pin header, 3 pins [form="♀ (female)"]
  PWM13 = LED - 5mm [color="Red (633nm)" package="5 mm [THT]"]
  SPI0 = JST PH SPI HEADER [form="♀ (female)" package=THT]
  Atmega1 = ATmega644 [part_number=ATmega1284p package=pdpi]
  C1 = Ceramic Capacitor [capacitance=100nF voltage=50V package="0805 [SMD, multilayer]"]
  C2 = Ceramic Capacitor [capacitance=100nF voltage=50V package="0805 [SMD, multilayer]"]
  XTAL = Crystal [frequency="16 MHz" package=THT]
  C10 = Ceramic Capacitor [capacitance=22pF voltage=50V package="0805 [SMD, multilayer]"]
  C11 = Ceramic Capacitor [capacitance=22pF voltage=50V package="0805 [SMD, multilayer]"]
  PWM14 = LED - 5mm [color="Red (633nm)" package="5 mm [THT]"]
  PWM15 = LED - 5mm [color="Red (633nm)" package="5 mm [THT]"]
  C12 = Ceramic Capacitor [capacitance=100nF voltage=50V package="0805 [SMD, multilayer]"]
  D1 = Diode [package=diode-1n4001]
  C14 = Ceramic Capacitor [capacitance=10µF voltage=50V package="0805 [SMD, multilayer]"]
  C13 = Ceramic Capacitor [capacitance=10µF voltage=50V package="0805 [SMD, multilayer]"]
  U1 = Voltage Regulator [package=78xxl]
  RN0 = female pin header, 10 pins [form="♀ (female)"]
  D0 = LED - 5mm [color="Red (633nm)" package="5 mm [THT]"]
  R1 = Resistor [tolerance=±5% resistance=10k package="0805 [SMD]"]
  J1 = female pin header, 10 pins [form="♀ (female)"]

nets:
  AGND/ATMEGA GND/GND: STEMMA.pin1, BAT1.V-, STEMMA1.GND, PWM(3).pin1, Part1.GND, PWM12.cathode, RESET.Pin_3, RESET.Pin_4, SPI1.GND, PWM(4).pin1, PWM13.cathode, SPI0.GND, Atmega1.GND, C1.0, C2.0, C10.1, C11.1, PWM14.cathode, PWM15.cathode, C12.0, C14.0, C13.0, U1.GND, RN0.pin1, D0.cathode
  5V/ATMEGA VCC/AVCC: STEMMA.pin2, STEMMA1.V+, PWM(3).pin2, Part1.VIN, SPI1.VCC, PWM(4).pin2, SPI0.VCC, Atmega1.VCC, Atmega1.AVCC, C1.1, C2.1, C14.1, U1.OUT, R1.Pin_1
  SDA: STEMMA.pin3, STEMMA1.SDA, Atmega1.PC1
  SCL: STEMMA.pin4, STEMMA1.SCL, Atmega1.PC0
  N1: BAT1.V+, D1.A
  N2: POWER.L1, D1.C
  N3: POWER.COM, C13.1, U1.IN
  PWM0: PWM(3).pin3, Atmega1.PB3
  DC: Part1.DC, Atmega1.PC4
  LCD RESET: Part1.RESET, Atmega1.PC5
  SDCS: Part1.SDCS, Atmega1.PC3
  LCD Enable: Part1.LCDCS, Atmega1.PC2
  MOSI: Part1.MOSI, SPI1.MOSI, SPI0.MOSI, Atmega1.PB5
  MISO: Part1.MISO, SPI1.MISO, SPI0.MISO, Atmega1.PB6
  SCK: Part1.SCLK, SPI1.SCK, SPI0.SCK, Atmega1.PB7
  LED0: PWM12.anode, Atmega1.PD4, RN0.pin2
  RESET: RESET.Pin_1, RESET.Pin_2, Atmega1.RESET, R1.Pin_0
  SPI1 Enable: SPI1.CS_, Atmega1.PC7
  PWM1: PWM(4).pin3, Atmega1.PB4
  LED1: PWM13.anode, Atmega1.PD5, RN0.pin3
  SPI0 Enable: SPI0.CS_, Atmega1.PC6
  LED4: Atmega1.PB0, RN0.pin6, D0.anode
  N4: Atmega1.PB1, J1.pin1
  N5: Atmega1.PB2, J1.pin2
  XTAL2: Atmega1.XTAL2, XTAL.pin_1, C11.0
  XTAL1: Atmega1.XTAL1, XTAL.pin_0, C10.0
  LED2: Atmega1.PD6, PWM14.anode, RN0.pin4
  LED3: Atmega1.PD7, PWM15.anode, RN0.pin5
  AREF: Atmega1.AREF, C12.1
  N6: Atmega1.PA7, J1.pin10
  N7: Atmega1.PA6, J1.pin9
  N8: Atmega1.PA5, J1.pin8
  N9: Atmega1.PA4, J1.pin7
  N10: Atmega1.PA3, J1.pin6
  N11: Atmega1.PA2, J1.pin5
  N12: Atmega1.PA1, J1.pin4
  N13: Atmega1.PA0, J1.pin3

notes:
  CRYSTAL
  "Hitagi" Expansion Board
  (C) 2020 Joshua Scoggins
  REV 6

custom parts:
  Adafruit Stemma 4 pin header: Adafruit STEMMA 4 pin header JST PH 4
  TFT 2.2 inch 320x240 w microSD: This lovely little display breakout is the best way to add a small, colorful and bright display to any project. Since the display uses 4-wire SPI to communicate and has its own pixel-addressable frame buffer, it can be used with every kind of microcontroller. Even a very small one with low memory and few pins available! The 2.2" display has 320x240 color pixels.
  JST PH SPI HEADER: Single device JST PH Based SPI Header
